// Logisim project Secuencias_minimizado.circ as structural Verilog: 17 circuits, main circuit main
module main (
  input  Clock,
  input  X,
  input  Reset,
  output S1,
  output S2,
  output S3
);

  wire Q0, Q1, Q2, Q3, R0, R1, R2, R3, S0, S1_t, S2_t, S3_t;

  S3_Simplificado s3_simplificado_1 (.Q3(Q3), .Q2(Q2), .Q1(Q1), .Q0(Q0), .S3(S3_t));
  R3_Simplificado r3_simplificado_1 (.Q3(Q3), .Q2(Q2), .Q1(Q1), .Q0(Q0), .X(X), .R3(R3));
  S2_Simplificado s2_simplificado_1 (.Q3(Q3), .Q2(Q2), .Q1(Q1), .Q0(Q0), .X(X), .S2(S2_t));
  R2_Simplificado r2_simplificado_1 (.Q3(Q3), .Q2(Q2), .Q1(Q1), .Q0(Q0), .X(X), .R2(R2));
  S1_Simplificado s1_simplificado_1 (.Q3(Q3), .Q2(Q2), .Q1(Q1), .Q0(Q0), .X(X), .S1(S1_t));
  R1_Simplificado r1_simplificado_1 (.Q3(Q3), .Q2(Q2), .Q1(Q1), .Q0(Q0), .X(X), .R1(R1));
  S0_Simplificado s0_simplificado_1 (.Q3(Q3), .Q2(Q2), .Q1(Q1), .Q0(Q0), .X(X), .S0(S0));
  R0_Simplificado r0_simplificado_1 (.Q3(Q3), .Q2(Q2), .Q1(Q1), .Q0(Q0), .X(X), .R0(R0));
  Z1_Simplificado z1_simplificado_1 (.Q3(Q3), .Q2(Q2), .Q0(Q0), .Z1(S1));
  Z2_Simplificado z2_simplificado_1 (.Q3(Q3), .Q2(Q2), .Q1(Q1), .Q0(Q0), .out_5(S2));
  Z3_Simplificado z3_simplificado_1 (.Q3(Q3), .Q2(Q2), .Q1(Q1), .Q0(Q0), .Z3(S3));
  S_R_Flip_Flop SR3 (.S(S3_t), .R(R3), .clk(Clock), .Q(Q3), .reset(Reset));  // open: Qn, preset
  S_R_Flip_Flop SR2 (.S(S2_t), .R(R2), .clk(Clock), .Q(Q2), .reset(Reset));  // open: Qn, preset
  S_R_Flip_Flop SR1 (.S(S1_t), .R(R1), .clk(Clock), .Q(Q1), .reset(Reset));  // open: Qn, preset
  S_R_Flip_Flop SR0 (.S(S0), .R(R0), .clk(Clock), .Q(Q0), .reset(Reset));  // open: Qn, preset
endmodule

module S3_Simplificado (
  input  Q3,
  input  Q2,
  input  Q1,
  input  Q0,
  output S3
);

  wire not_1_out, not_2_out;

  not not_1 (not_1_out, Q3);
  not not_2 (not_2_out, Q1);
  and and_1 (S3, not_1_out, Q2, not_2_out, Q0);
endmodule

module R3_Simplificado (
  input  Q3,
  input  Q2,
  input  Q1,
  input  Q0,
  input  X,
  output R3
);

  wire and_1_out, and_2_out, and_3_out, not_1_out, not_2_out, or_1_out;

  not not_1 (not_1_out, Q0);
  not not_2 (not_2_out, X);
  and and_1 (and_1_out, Q3, Q2, Q0, X);
  and and_2 (and_2_out, Q2, Q1, not_2_out);
  and and_3 (and_3_out, Q2, not_1_out, not_2_out);
  or or_1 (or_1_out, and_2_out, and_3_out);
  or or_2 (R3, and_1_out, or_1_out);
endmodule

module S2_Simplificado (
  input  Q3,
  input  Q2,
  input  Q1,
  input  Q0,
  input  X,
  output S2
);

  wire and_1_out, and_2_out, not_1_out, not_2_out, not_3_out, not_4_out;

  not not_1 (not_1_out, Q3);
  not not_2 (not_2_out, Q2);
  not not_3 (not_3_out, Q0);
  not not_4 (not_4_out, X);
  and and_1 (and_1_out, not_1_out, not_2_out, Q1, not_3_out);
  and and_2 (and_2_out, not_1_out, not_2_out, Q1, not_4_out);
  or or_1 (S2, and_1_out, and_2_out);
endmodule

module R2_Simplificado (
  input  Q3,
  input  Q2,
  input  Q1,
  input  Q0,
  input  X,
  output R2
);

  wire and_1_out, and_2_out, and_3_out, not_1_out, not_2_out, or_1_out;

  not not_1 (not_1_out, Q3);
  not not_2 (not_2_out, Q0);
  and and_1 (and_1_out, not_1_out, Q2, not_2_out);
  and and_2 (and_2_out, Q3, Q2, Q1, Q0);
  and and_3 (and_3_out, not_1_out, Q2, Q1, X);
  or or_1 (or_1_out, and_1_out, and_3_out);
  or or_2 (R2, or_1_out, and_2_out);
endmodule

module S1_Simplificado (
  input  Q3,
  input  Q2,
  input  Q1,
  input  Q0,
  input  X,
  output S1
);

  wire and_1_out, and_2_out, and_3_out, not_1_out, not_2_out, not_3_out, not_4_out, not_5_out, or_1_out;

  not not_1 (not_1_out, Q2);
  not not_2 (not_2_out, Q3);
  not not_3 (not_3_out, Q1);
  not not_4 (not_4_out, Q0);
  not not_5 (not_5_out, X);
  and and_1 (and_1_out, not_2_out, not_1_out, not_3_out, Q0);
  and and_2 (and_2_out, Q3, Q2, not_3_out, not_4_out);
  and and_3 (and_3_out, Q3, Q2, not_3_out, not_5_out);
  or or_1 (or_1_out, and_1_out, and_2_out);
  or or_2 (S1, or_1_out, and_3_out);
endmodule

module R1_Simplificado (
  input  Q3,
  input  Q2,
  input  Q1,
  input  Q0,
  input  X,
  output R1
);

  wire and_1_out, and_2_out, and_3_out, not_1_out, not_2_out, not_3_out, or_1_out;

  not not_1 (not_1_out, Q0);
  not not_2 (not_2_out, Q3);
  not not_3 (not_3_out, X);
  and and_1 (and_1_out, not_2_out, Q2);
  and and_2 (and_2_out, not_2_out, Q1, X);
  and and_3 (and_3_out, Q2, Q1, not_1_out, not_3_out);
  or or_1 (or_1_out, and_1_out, and_2_out);
  or or_2 (R1, or_1_out, and_3_out);
endmodule

module S0_Simplificado (
  input  Q3,
  input  Q2,
  input  Q1,
  input  Q0,
  input  X,
  output S0
);

  wire and_1_out, and_2_out, and_3_out, not_1_out, not_2_out, not_3_out, not_4_out, not_5_out, or_1_out;

  not not_1 (not_1_out, Q3);
  not not_2 (not_2_out, Q0);
  not not_3 (not_3_out, Q0);
  not not_4 (not_4_out, Q2);
  not not_5 (not_5_out, Q0);
  and and_1 (and_1_out, not_1_out, not_2_out, X);
  and and_2 (and_2_out, Q2, not_3_out, X);
  and and_3 (and_3_out, not_1_out, not_4_out, Q1, not_5_out);
  or or_1 (or_1_out, and_1_out, and_2_out);
  or or_2 (S0, or_1_out, and_3_out);
endmodule

module R0_Simplificado (
  input  Q3,
  input  Q2,
  input  Q1,
  input  Q0,
  input  X,
  output R0
);

  wire and_1_out, and_2_out, and_3_out, and_4_out, not_1_out, not_2_out, not_3_out, not_4_out, not_5_out,
       not_6_out, or_1_out, or_2_out;

  not not_1 (not_1_out, Q1);
  not not_2 (not_2_out, X);
  not not_3 (not_3_out, Q3);
  not not_4 (not_4_out, X);
  not not_5 (not_5_out, Q1);
  not not_6 (not_6_out, Q1);
  and and_1 (and_1_out, Q2, not_1_out, not_2_out);
  and and_2 (and_2_out, not_3_out, Q1, Q0, not_4_out);
  and and_3 (and_3_out, not_1_out, not_5_out, not_6_out, Q0, X);
  and and_4 (and_4_out, Q3, Q2, Q1, Q0, X);
  or or_1 (or_1_out, and_1_out, and_2_out);
  or or_2 (or_2_out, and_3_out, and_4_out);
  or or_3 (R0, or_1_out, or_2_out);
endmodule

module Z1_Simplificado (
  input  Q3,
  input  Q2,
  input  Q0,
  output Z1
);

  wire not_1_out, not_2_out;

  not not_1 (not_1_out, Q3);
  not not_2 (not_2_out, Q0);
  and and_1 (Z1, not_1_out, Q2, not_2_out);
endmodule

module Z2_Simplificado (
  input  Q3,
  input  Q2,
  input  Q1,
  input  Q0,
  output out_5
);

  wire not_1_out, not_2_out, not_3_out;

  not not_1 (not_1_out, Q3);
  not not_2 (not_2_out, Q1);
  not not_3 (not_3_out, Q0);
  and and_1 (out_5, not_1_out, Q2, not_2_out, not_3_out);
endmodule

module Z3_Simplificado (
  input  Q3,
  input  Q2,
  input  Q1,
  input  Q0,
  output Z3
);

  and and_1 (Z3, Q3, Q2, Q1, Q0);
endmodule

module circuito (
);

  wire CLK_out, main_1_s1, main_1_s2, main_1_s3, random_1_out, RESET_out, sevensegmentdisplay_1_a,
       sevensegmentdisplay_1_b, sevensegmentdisplay_1_c, sevensegmentdisplay_1_d, sevensegmentdisplay_1_e,
       sevensegmentdisplay_1_f, sevensegmentdisplay_1_g, sevensegmentdisplay_2_a, sevensegmentdisplay_2_b,
       sevensegmentdisplay_2_c, sevensegmentdisplay_2_d, sevensegmentdisplay_2_e, sevensegmentdisplay_2_f,
       sevensegmentdisplay_2_g, sevensegmentdisplay_3_a, sevensegmentdisplay_3_b, sevensegmentdisplay_3_c,
       sevensegmentdisplay_3_d, sevensegmentdisplay_3_e, sevensegmentdisplay_3_f, sevensegmentdisplay_3_g,
       sevensegmentdisplay_4_a, sevensegmentdisplay_4_b, sevensegmentdisplay_4_c, sevensegmentdisplay_4_d,
       sevensegmentdisplay_4_e, sevensegmentdisplay_4_f, sevensegmentdisplay_4_g, sevensegmentdisplay_5_a,
       sevensegmentdisplay_5_b, sevensegmentdisplay_5_c, sevensegmentdisplay_5_d, sevensegmentdisplay_5_e,
       sevensegmentdisplay_5_f, sevensegmentdisplay_5_g, sevensegmentdisplay_6_a, sevensegmentdisplay_6_b,
       sevensegmentdisplay_6_c, sevensegmentdisplay_6_d, sevensegmentdisplay_6_e, sevensegmentdisplay_6_f,
       sevensegmentdisplay_6_g, sevensegmentdisplay_7_a, sevensegmentdisplay_7_b, sevensegmentdisplay_7_c,
       sevensegmentdisplay_7_d, sevensegmentdisplay_7_e, sevensegmentdisplay_7_f, sevensegmentdisplay_7_g,
       sevensegmentdisplay_8_a, sevensegmentdisplay_8_b, sevensegmentdisplay_8_c, sevensegmentdisplay_8_d,
       sevensegmentdisplay_8_e, sevensegmentdisplay_8_f, sevensegmentdisplay_8_g, sevensegmentdisplay_9_a,
       sevensegmentdisplay_9_b, sevensegmentdisplay_9_c, sevensegmentdisplay_9_d, sevensegmentdisplay_9_e,
       sevensegmentdisplay_9_f, sevensegmentdisplay_9_g;
  wire [1:0] binarytobcd_1_centena, binarytobcd_2_centena, binarytobcd_3_centena;
  wire [3:0] binarytobcd_1_decena, binarytobcd_1_unidades, binarytobcd_2_decena, binarytobcd_2_unidades,
       binarytobcd_3_decena, binarytobcd_3_unidades;
  wire [7:0] contador_eventos_1_out_4, contador_eventos_2_out_4, contador_eventos_3_out_4;

  Clock CLK (.out(CLK_out));
  Button RESET (.out(RESET_out));
  Random #(.width(1)) random_1 (.clr(RESET_out), .clk(CLK_out), .out(random_1_out));  // open: next
  main main_1 (.Clock(CLK_out), .X(random_1_out), .Reset(RESET_out), .S1(main_1_s1), .S2(main_1_s2), .S3(main_1_s3));
  contador_eventos contador_eventos_1 (
    .Reset(RESET_out), .Switch(main_1_s3), .CLK(CLK_out), .out_4(contador_eventos_1_out_4));
  contador_eventos contador_eventos_2 (
    .Reset(RESET_out), .Switch(main_1_s1), .CLK(CLK_out), .out_4(contador_eventos_2_out_4));
  // Probe on contador_eventos_2_out_4
  contador_eventos contador_eventos_3 (
    .Reset(RESET_out), .Switch(main_1_s2), .CLK(CLK_out), .out_4(contador_eventos_3_out_4));
  BinaryToBCD binarytobcd_1 (
    .in_1(contador_eventos_1_out_4), .Centena(binarytobcd_1_centena), .Decena(binarytobcd_1_decena),
    .Unidades(binarytobcd_1_unidades));
  // Probe on binarytobcd_1_centena
  // Probe on binarytobcd_1_decena
  // Probe on binarytobcd_1_unidades
  BinaryToBCD binarytobcd_2 (
    .in_1(contador_eventos_2_out_4), .Centena(binarytobcd_2_centena), .Decena(binarytobcd_2_decena),
    .Unidades(binarytobcd_2_unidades));
  // Probe on binarytobcd_2_unidades
  BinaryToBCD binarytobcd_3 (
    .in_1(contador_eventos_3_out_4), .Centena(binarytobcd_3_centena), .Decena(binarytobcd_3_decena),
    .Unidades(binarytobcd_3_unidades));
  // Probe on binarytobcd_2_centena
  // Probe on binarytobcd_2_decena
  // Probe on binarytobcd_3_centena
  // Probe on binarytobcd_3_decena
  // Probe on binarytobcd_3_unidades
  SevenSegmentDisplay sevensegmentdisplay_1 (
    .E1(binarytobcd_1_centena[0]), .E2(binarytobcd_1_centena[1]), .g(sevensegmentdisplay_1_g),
    .a(sevensegmentdisplay_1_a), .b(sevensegmentdisplay_1_b), .f(sevensegmentdisplay_1_f),
    .e(sevensegmentdisplay_1_e), .d(sevensegmentdisplay_1_d), .c(sevensegmentdisplay_1_c));  // open: E3, E4
  SevenSegmentDisplay sevensegmentdisplay_2 (
    .E1(binarytobcd_1_decena[0]), .E2(binarytobcd_1_decena[1]), .E3(binarytobcd_1_decena[2]),
    .E4(binarytobcd_1_decena[3]), .g(sevensegmentdisplay_2_g), .a(sevensegmentdisplay_2_a),
    .b(sevensegmentdisplay_2_b), .f(sevensegmentdisplay_2_f), .e(sevensegmentdisplay_2_e),
    .d(sevensegmentdisplay_2_d), .c(sevensegmentdisplay_2_c));
  _7_Segment_Display u_7_segment_display_1 (
    .g(sevensegmentdisplay_1_g), .f(sevensegmentdisplay_1_f), .a(sevensegmentdisplay_1_a),
    .b(sevensegmentdisplay_1_b), .e(sevensegmentdisplay_1_e), .d(sevensegmentdisplay_1_d),
    .c(sevensegmentdisplay_1_c));  // open: dp
  _7_Segment_Display u_7_segment_display_2 (
    .g(sevensegmentdisplay_2_g), .f(sevensegmentdisplay_2_f), .a(sevensegmentdisplay_2_a),
    .b(sevensegmentdisplay_2_b), .e(sevensegmentdisplay_2_e), .d(sevensegmentdisplay_2_d),
    .c(sevensegmentdisplay_2_c));  // open: dp
  SevenSegmentDisplay sevensegmentdisplay_3 (
    .E1(binarytobcd_1_unidades[0]), .E2(binarytobcd_1_unidades[1]), .E3(binarytobcd_1_unidades[2]),
    .E4(binarytobcd_1_unidades[3]), .g(sevensegmentdisplay_3_g), .a(sevensegmentdisplay_3_a),
    .b(sevensegmentdisplay_3_b), .f(sevensegmentdisplay_3_f), .e(sevensegmentdisplay_3_e),
    .d(sevensegmentdisplay_3_d), .c(sevensegmentdisplay_3_c));
  _7_Segment_Display u_7_segment_display_3 (
    .g(sevensegmentdisplay_3_g), .f(sevensegmentdisplay_3_f), .a(sevensegmentdisplay_3_a),
    .b(sevensegmentdisplay_3_b), .e(sevensegmentdisplay_3_e), .d(sevensegmentdisplay_3_d),
    .c(sevensegmentdisplay_3_c));  // open: dp
  SevenSegmentDisplay sevensegmentdisplay_4 (
    .E1(binarytobcd_2_centena[0]), .E2(binarytobcd_2_centena[1]), .g(sevensegmentdisplay_4_g),
    .a(sevensegmentdisplay_4_a), .b(sevensegmentdisplay_4_b), .f(sevensegmentdisplay_4_f),
    .e(sevensegmentdisplay_4_e), .d(sevensegmentdisplay_4_d), .c(sevensegmentdisplay_4_c));  // open: E3, E4
  SevenSegmentDisplay sevensegmentdisplay_5 (
    .E1(binarytobcd_2_decena[0]), .E2(binarytobcd_2_decena[1]), .E3(binarytobcd_2_decena[2]),
    .E4(binarytobcd_2_decena[3]), .g(sevensegmentdisplay_5_g), .a(sevensegmentdisplay_5_a),
    .b(sevensegmentdisplay_5_b), .f(sevensegmentdisplay_5_f), .e(sevensegmentdisplay_5_e),
    .d(sevensegmentdisplay_5_d), .c(sevensegmentdisplay_5_c));
  SevenSegmentDisplay sevensegmentdisplay_6 (
    .E1(binarytobcd_2_unidades[0]), .E2(binarytobcd_2_unidades[1]), .E3(binarytobcd_2_unidades[2]),
    .E4(binarytobcd_2_unidades[3]), .g(sevensegmentdisplay_6_g), .a(sevensegmentdisplay_6_a),
    .b(sevensegmentdisplay_6_b), .f(sevensegmentdisplay_6_f), .e(sevensegmentdisplay_6_e),
    .d(sevensegmentdisplay_6_d), .c(sevensegmentdisplay_6_c));
  SevenSegmentDisplay sevensegmentdisplay_7 (
    .E1(binarytobcd_3_centena[0]), .E2(binarytobcd_3_centena[1]), .g(sevensegmentdisplay_7_g),
    .a(sevensegmentdisplay_7_a), .b(sevensegmentdisplay_7_b), .f(sevensegmentdisplay_7_f),
    .e(sevensegmentdisplay_7_e), .d(sevensegmentdisplay_7_d), .c(sevensegmentdisplay_7_c));  // open: E3, E4
  _7_Segment_Display u_7_segment_display_4 (
    .g(sevensegmentdisplay_4_g), .f(sevensegmentdisplay_4_f), .a(sevensegmentdisplay_4_a),
    .b(sevensegmentdisplay_4_b), .e(sevensegmentdisplay_4_e), .d(sevensegmentdisplay_4_d),
    .c(sevensegmentdisplay_4_c));  // open: dp
  _7_Segment_Display u_7_segment_display_5 (
    .g(sevensegmentdisplay_5_g), .f(sevensegmentdisplay_5_f), .a(sevensegmentdisplay_5_a),
    .b(sevensegmentdisplay_5_b), .e(sevensegmentdisplay_5_e), .d(sevensegmentdisplay_5_d),
    .c(sevensegmentdisplay_5_c));  // open: dp
  _7_Segment_Display u_7_segment_display_6 (
    .g(sevensegmentdisplay_6_g), .f(sevensegmentdisplay_6_f), .a(sevensegmentdisplay_6_a),
    .b(sevensegmentdisplay_6_b), .e(sevensegmentdisplay_6_e), .d(sevensegmentdisplay_6_d),
    .c(sevensegmentdisplay_6_c));  // open: dp
  _7_Segment_Display u_7_segment_display_7 (
    .g(sevensegmentdisplay_7_g), .f(sevensegmentdisplay_7_f), .a(sevensegmentdisplay_7_a),
    .b(sevensegmentdisplay_7_b), .e(sevensegmentdisplay_7_e), .d(sevensegmentdisplay_7_d),
    .c(sevensegmentdisplay_7_c));  // open: dp
  SevenSegmentDisplay sevensegmentdisplay_8 (
    .E1(binarytobcd_3_decena[0]), .E2(binarytobcd_3_decena[1]), .E3(binarytobcd_3_decena[2]),
    .E4(binarytobcd_3_decena[3]), .g(sevensegmentdisplay_8_g), .a(sevensegmentdisplay_8_a),
    .b(sevensegmentdisplay_8_b), .f(sevensegmentdisplay_8_f), .e(sevensegmentdisplay_8_e),
    .d(sevensegmentdisplay_8_d), .c(sevensegmentdisplay_8_c));
  _7_Segment_Display u_7_segment_display_8 (
    .g(sevensegmentdisplay_8_g), .f(sevensegmentdisplay_8_f), .a(sevensegmentdisplay_8_a),
    .b(sevensegmentdisplay_8_b), .e(sevensegmentdisplay_8_e), .d(sevensegmentdisplay_8_d),
    .c(sevensegmentdisplay_8_c));  // open: dp
  SevenSegmentDisplay sevensegmentdisplay_9 (
    .E1(binarytobcd_3_unidades[0]), .E2(binarytobcd_3_unidades[1]), .E3(binarytobcd_3_unidades[2]),
    .E4(binarytobcd_3_unidades[3]), .g(sevensegmentdisplay_9_g), .a(sevensegmentdisplay_9_a),
    .b(sevensegmentdisplay_9_b), .f(sevensegmentdisplay_9_f), .e(sevensegmentdisplay_9_e),
    .d(sevensegmentdisplay_9_d), .c(sevensegmentdisplay_9_c));
  _7_Segment_Display u_7_segment_display_9 (
    .g(sevensegmentdisplay_9_g), .f(sevensegmentdisplay_9_f), .a(sevensegmentdisplay_9_a),
    .b(sevensegmentdisplay_9_b), .e(sevensegmentdisplay_9_e), .d(sevensegmentdisplay_9_d),
    .c(sevensegmentdisplay_9_c));  // open: dp
endmodule

module contador_eventos (
  input  Reset,
  input  Switch,
  input  CLK,
  output [7:0] out_4
);

  wire and_1_out, d_ff_1_qn, d_ff_2_qn, d_ff_3_qn, d_ff_4_qn, d_ff_5_qn, d_ff_6_qn, d_ff_7_qn, d_ff_8_qn,
       not_1_out;

  not not_1 (not_1_out, CLK);
  and and_1 (and_1_out, Switch, not_1_out);
  D_Flip_Flop d_ff_1 (.D(d_ff_1_qn), .clk(and_1_out), .Q(out_4[0]), .Qn(d_ff_1_qn), .reset(Reset));  // open: preset
  D_Flip_Flop d_ff_2 (.D(d_ff_2_qn), .clk(d_ff_7_qn), .Q(out_4[4]), .Qn(d_ff_2_qn), .reset(Reset));  // open: preset
  D_Flip_Flop d_ff_3 (.D(d_ff_3_qn), .clk(d_ff_1_qn), .Q(out_4[1]), .Qn(d_ff_3_qn), .reset(Reset));  // open: preset
  D_Flip_Flop d_ff_4 (.D(d_ff_4_qn), .clk(d_ff_2_qn), .Q(out_4[5]), .Qn(d_ff_4_qn), .reset(Reset));  // open: preset
  D_Flip_Flop d_ff_5 (.D(d_ff_5_qn), .clk(d_ff_3_qn), .Q(out_4[2]), .Qn(d_ff_5_qn), .reset(Reset));  // open: preset
  D_Flip_Flop d_ff_6 (.D(d_ff_6_qn), .clk(d_ff_4_qn), .Q(out_4[6]), .Qn(d_ff_6_qn), .reset(Reset));  // open: preset
  D_Flip_Flop d_ff_7 (.D(d_ff_7_qn), .clk(d_ff_5_qn), .Q(out_4[3]), .Qn(d_ff_7_qn), .reset(Reset));  // open: preset
  D_Flip_Flop d_ff_8 (.D(d_ff_8_qn), .clk(d_ff_6_qn), .Q(out_4[7]), .Qn(d_ff_8_qn), .reset(Reset));  // open: preset
  // Probe on out_4
endmodule

module SevenSegmentDisplay (
  input  E1,
  input  E2,
  input  E3,
  input  E4,
  output g,
  output a,
  output b,
  output f,
  output e,
  output d,
  output c
);

  wire and_1_out, and_2_out, and_3_out, and_4_out, and_5_out, and_6_out, and_7_out, and_8_out, and_9_out,
       and_10_out, and_11_out, and_12_out, and_13_out, and_14_out, and_15_out, and_16_out, and_17_out,
       and_18_out, not_1_out, not_2_out, not_3_out, not_4_out, not_5_out, not_6_out, not_7_out, not_8_out,
       not_9_out, not_10_out, not_11_out, not_12_out, not_13_out, not_14_out, not_15_out, not_16_out,
       not_17_out;

  not not_1 (not_1_out, E1);
  not not_2 (not_2_out, E3);
  not not_3 (not_3_out, E1);
  not not_4 (not_4_out, E2);
  not not_5 (not_5_out, E3);
  not not_6 (not_6_out, E2);
  not not_7 (not_7_out, E4);
  not not_8 (not_8_out, E1);
  not not_9 (not_9_out, E2);
  not not_10 (not_10_out, E3);
  not not_11 (not_11_out, E1);
  not not_12 (not_12_out, E3);
  not not_13 (not_13_out, E1);
  not not_14 (not_14_out, E2);
  not not_15 (not_15_out, E1);
  not not_16 (not_16_out, E2);
  not not_17 (not_17_out, E3);
  and and_1 (and_1_out, not_1_out, not_2_out);
  and and_2 (and_2_out, E1, E3);
  and and_3 (and_3_out, not_3_out, not_4_out);
  and and_4 (and_4_out, E1, E2);
  and and_5 (and_5_out, E2, E3);
  and and_6 (and_6_out, E1, not_7_out);
  and and_7 (and_7_out, not_8_out, not_10_out);
  and and_8 (and_8_out, E3, not_9_out, E1);
  and and_9 (and_9_out, not_11_out, E2);
  and and_10 (and_10_out, not_11_out, not_12_out);
  and and_11 (and_11_out, E3, not_13_out);
  and and_12 (and_12_out, not_13_out, not_14_out);
  and and_13 (and_13_out, E3, not_14_out);
  and and_14 (and_14_out, not_16_out, E3);
  and and_15 (and_15_out, not_15_out, E2);
  and and_16 (and_16_out, not_17_out, E2);
  or or_1 (a, and_1_out, and_2_out, E2, E4);
  or or_2 (b, and_3_out, not_5_out, and_4_out);
  or or_3 (c, and_5_out, not_6_out, and_6_out);
  and and_17 (and_17_out, E2, not_10_out);
  and and_18 (and_18_out, not_8_out, E2);
  or or_4 (e, and_9_out, and_10_out);
  or or_5 (f, and_11_out, E4, and_12_out, and_13_out);
  or or_6 (d, and_7_out, and_17_out, and_8_out, and_18_out, E4);
  or or_7 (g, and_14_out, and_15_out, and_16_out, E4);
  _7_Segment_Display u_7_segment_display_1 (.g(g), .f(f), .a(a), .b(b), .e(e), .d(d), .c(c));  // open: dp

  // Notes on the sheet:
  //   segmento b
  //   segmento a
  //   segmento c
  //   segmento d
  //   segmento e
  //   segmento f
  //   segmento g
endmodule

module Sum (
  input  b3,
  input  b2,
  input  b1,
  input  b0,
  output p3,
  output p2,
  output p1,
  output p0
);

  wire and_1_out, and_2_out, and_3_out, and_4_out, and_5_out, and_6_out, and_7_out, and_8_out, and_9_out,
       and_10_out, and_11_out, not_1_out, not_2_out, not_3_out, not_4_out, not_5_out, not_6_out, not_7_out,
       not_8_out;

  and and_1 (and_1_out, b2, b0);
  and and_2 (and_2_out, b2, b1);
  not not_1 (not_1_out, b1);
  and and_3 (and_3_out, b2, not_1_out, not_2_out);
  not not_2 (not_2_out, b0);
  and and_4 (and_4_out, b3, b0);
  and and_5 (and_5_out, b3, b2);
  not not_3 (not_3_out, b2);
  and and_6 (and_6_out, not_3_out, b1);
  and and_7 (and_7_out, b1, b0);
  and and_8 (and_8_out, b3, not_4_out);
  not not_4 (not_4_out, b0);
  not not_5 (not_5_out, b3);
  and and_9 (and_9_out, not_5_out, not_6_out, b0);
  not not_6 (not_6_out, b2);
  and and_10 (and_10_out, b2, b1, not_7_out);
  not not_7 (not_7_out, b0);
  and and_11 (and_11_out, b3, not_8_out);
  not not_8 (not_8_out, b0);
  or or_1 (p3, and_1_out, and_2_out, b3);
  or or_2 (p2, and_3_out, and_4_out, and_5_out);
  or or_3 (p1, and_6_out, and_7_out, and_8_out);
  or or_4 (p0, and_9_out, and_10_out, and_11_out);
endmodule

module BinaryToBCD (
  input  [7:0] in_1,
  output [1:0] Centena,
  output [3:0] Decena,
  output [3:0] Unidades
);

  wire sum_1_p0, sum_1_p1, sum_1_p2, sum_1_p3, sum_2_p0, sum_2_p1, sum_2_p2, sum_2_p3, sum_3_p0, sum_3_p1,
       sum_3_p2, sum_3_p3, sum_4_p0, sum_4_p1, sum_4_p2, sum_5_p0, sum_5_p1, sum_5_p2, sum_5_p3;

  Sum sum_1 (
    .b2(in_1[7]), .b1(in_1[6]), .b0(in_1[5]), .p3(sum_1_p3), .p2(sum_1_p2), .p1(sum_1_p1), .p0(sum_1_p0));  // open: b3
  Sum sum_2 (
    .b3(sum_1_p2), .b2(sum_1_p1), .b1(sum_1_p0), .b0(in_1[4]), .p3(sum_2_p3), .p2(sum_2_p2), .p1(sum_2_p1),
    .p0(sum_2_p0));
  Sum sum_3 (
    .b3(sum_2_p2), .b2(sum_2_p1), .b1(sum_2_p0), .b0(in_1[3]), .p3(sum_3_p3), .p2(sum_3_p2), .p1(sum_3_p1),
    .p0(sum_3_p0));
  Sum sum_4 (
    .b2(sum_1_p3), .b1(sum_2_p3), .b0(sum_3_p3), .p3(Centena[1]), .p2(sum_4_p2), .p1(sum_4_p1), .p0(sum_4_p0));  // open: b3
  Sum sum_5 (
    .b3(sum_3_p2), .b2(sum_3_p1), .b1(sum_3_p0), .b0(in_1[2]), .p3(sum_5_p3), .p2(sum_5_p2), .p1(sum_5_p1),
    .p0(sum_5_p0));
  // Probe on Centena
  Sum sum_6 (
    .b3(sum_4_p2), .b2(sum_4_p1), .b1(sum_4_p0), .b0(sum_5_p3), .p3(Centena[0]), .p2(Decena[3]),
    .p1(Decena[2]), .p0(Decena[1]));
  Sum sum_7 (
    .b3(sum_5_p2), .b2(sum_5_p1), .b1(sum_5_p0), .b0(in_1[1]), .p3(Decena[0]), .p2(Unidades[3]),
    .p1(Unidades[2]), .p0(Unidades[1]));
  // Probe on {Unidades[3:1], in_1[0]}
  // Probe on Decena

  assign Unidades[0] = in_1[0];
endmodule
